# Fritzing sketch forrasztó (saved by Fritzing 0.9.6b)
circuit board: 8.92476cm x 5.16853cm
breadboards: 1

parts:
  Arduino_nano = Arduino Nano (Rev3.0)
  LM_358 = LM 358 Dual Op-Amp [package="DIP8 [THT]"]
  1_2K = Resistor [tolerance=±5% power=0.25 resistance=220 package=THT]
  DC-DC = SBX DSUN [package=THT]
  Gnd_+5v_SCL_SDA = rounded female pin header, 4 pins [form="♀ (female rounded)"]
  part = longpad pin header, 4 pins [form="long pad"]  # not connected
  Pot_10k = longpad pin header, 3 pins [form="long pad"]
  Q1 = Basic FET P-Channel [package="TO220 [THT]"]
  1N4007 = Rectifier Diode [part_number=1N4001 package="300 mil [THT]"]
  +_24v_- = screw terminal, 2 pins
  Iron = screw terminal, 2 pins
  10k = Resistor [tolerance=±5% power=0.25 resistance=220 package=THT]
  part_2 = longpad pin header, 4 pins [form="long pad"]  # not connected
  part_3 = longpad pin header, 4 pins [form="long pad"]  # not connected
  part_4 = longpad pin header, 15 pins [form="long pad"]  # not connected
  IRFZ44N = Voltage Regulator [package=to-220-alt]
  J9 = longpad pin header, 15 pins [form="long pad"]  # not connected
  LED1 = LED - 5mm [color="Red (633nm)" current=0.030 package="5 mm [THT]"]
  R4 = Resistor [tolerance=±5% power=0.25 resistance=220 package=THT]
  +_Sensor_- = screw terminal, 2 pins
  Pot_270K = Trimmer Potentiometer [maximum_resistance=10kΩ package=THT]
  part_5 = longpad pin header, 1 pin [form="long pad"]  # not connected
  part_6 = longpad pin header, 1 pin [form="long pad"]
  part_7 = longpad pin header, 1 pin [form="long pad"]  # not connected
  part_8 = longpad pin header, 1 pin [form="long pad"]  # not connected
  part_9 = longpad pin header, 1 pin [form="long pad"]  # not connected
  part_10 = longpad pin header, 1 pin [form="long pad"]  # not connected
  part_11 = longpad pin header, 1 pin [form="long pad"]  # not connected
  part_12 = longpad pin header, 1 pin [form="long pad"]  # not connected
  part_13 = longpad pin header, 1 pin [form="long pad"]  # not connected
  part_14 = longpad pin header, 1 pin [form="long pad"]  # not connected
  part_15 = longpad pin header, 1 pin [form="long pad"]  # not connected

nets:
  N1: Arduino_nano.GND, DC-DC.+VIN
  N2: Arduino_nano.D7, LED1.cathode
  N3: Arduino_nano.D10, 10k.Pin_1, IRFZ44N.IN
  VIN: Arduino_nano.VIN, DC-DC.GND, 1N4007.cathode, +_24v_-.pin2, Iron.pin2
  N4: Arduino_nano.5V, LM_358.connector7, Gnd_+5v_SCL_SDA.pin2, Pot_10k.pin3
  N5: Arduino_nano.A5, Gnd_+5v_SCL_SDA.pin3
  N6: Arduino_nano.A4, Gnd_+5v_SCL_SDA.pin4
  N7: Arduino_nano.A3, Pot_10k.pin2
  N8: Arduino_nano.A1, LM_358.connector0, Pot_270K.wiper
  N9: LM_358.connector1, 1_2K.Pin_0, Pot_270K.leg2, part_6.pin1
  N10: LM_358.connector2, +_Sensor_-.pin2
  N11: LM_358.connector3, DC-DC.+VOUT, Gnd_+5v_SCL_SDA.pin1, Pot_10k.pin1, Q1.source, +_24v_-.pin1, 10k.Pin_0, R4.Pin_0, +_Sensor_-.pin1
  N12: 1N4007.anode, Iron.pin1, IRFZ44N.GND
  N13: LED1.anode, R4.Pin_1

notes:
  +IN
  +
  -IN
  -

custom parts:
  SBX DSUN: SBX DSUN input voltage 4.5 - 28V DC output voltage .8v to 20VDC (step down converter) Output current 3A max
